# Fritzing sketch iot-car (saved by Fritzing 0.9.3b)
breadboards: 2

parts:
  S1 = H-Bridge with L298N
  BATT1 = 4xAA Switchable Battery Pack w/Bare Wire
  M1 = DC Motor
  M2 = DC Motor
  M3 = DC Motor
  M4 = DC Motor
  U2 = NodeMCU V3.0
  hc-sr1 = hc-sr04
  R4 = Resistor [tolerance=±5% resistance=220 package="0402 [SMD]"]
  R5 = Resistor [tolerance=±5% resistance=220 package="0402 [SMD]"]
  R6 = Resistor [tolerance=±5% resistance=220 package="0402 [SMD]"]
  LED2 = RGB LED - (4 legs) [package="5 mm [THT]"]

nets:
  N1: S1.12V, BATT1.POS
  GND: S1.GND, BATT1.NEG, U2.GND#6, U2.GND#13, U2.GND#16, U2.GND#33, hc-sr1.GND, LED2.common_anode
  N2: S1.ENA, S1.ENB, U2.D0
  N3: S1.IN1, S1.IN3, U2.D4
  N4: S1.IN2, S1.IN4, U2.D3
  N5: S1.M1-01, M3.pin_2, M4.pin_2
  N6: S1.M1-02, M3.pin_1, M4.pin_1
  N7: S1.M2-01, M1.pin_2, M2.pin_2
  N8: S1.M2-02, M1.pin_1, M2.pin_1
  N9: U2.D1, hc-sr1.Echo
  N10: U2.D2, hc-sr1.Trig
  N11: U2.D5, R6.Pin_0
  N12: U2.D6, R5.Pin_0
  N13: U2.D7, R4.Pin_0
  VIN: U2.Vin, hc-sr1.VCC
  N14: R4.Pin_1, LED2.blue_cathode
  N15: R5.Pin_1, LED2.green_cathode
  N16: R6.Pin_1, LED2.red_cathode

custom parts:
  H-Bridge with L298N: h-bridge
  4xAA Switchable Battery Pack w/Bare Wire: 4xAA Switchable Battery Pack with Bare Wire connection
  NodeMCU V3.0: ESP8266 based NodeMCU
